# Fritzing sketch Wiring For Voice Control Robot With Sensor (saved by Fritzing 0.9.3b)
breadboards: 1

parts:
  U1 = NodeMCU V1.0
  IC1 = L293D [package=THT]
  LEFT_Motor = DC Motor
  S1 = Pushbutton [package="[SMD]"]
  RIGHT_Motor = DC Motor
  VCC1 = 4 x AAA Battery Mount
  ULTRASONIC_DISTANCE_SENSOR = hc-sr04

nets:
  GND: U1.D0, U1.GND, IC1.0V, S1.Pin_1, S1.Pin_2, VCC1.-, ULTRASONIC_DISTANCE_SENSOR.GND
  N1: U1.D1, ULTRASONIC_DISTANCE_SENSOR.Trig
  N2: U1.D2, ULTRASONIC_DISTANCE_SENSOR.Echo
  N3: U1.D3, IC1.In_2
  N4: U1.D4, IC1.In_1
  N5: U1.D6, IC1.Enable_1
  N6: U1.D7, IC1.In_4
  N7: U1.D8, IC1.In_3
  N8: U1.Vin, IC1.+V
  N9: IC1.Out_1_(_Controlled_by_Enable_1_), IC1.Out_2_(_Controlled_by_Enable_1_), LEFT_Motor.pin_1, LEFT_Motor.pin_2
  N10: IC1.+Vmotor, VCC1.+, ULTRASONIC_DISTANCE_SENSOR.VCC
  N11: IC1.Out_3_(_Controlled_by_Enable_2_), IC1.Out_4_(_Controlled_by_Enable_2_), RIGHT_Motor.pin_1, RIGHT_Motor.pin_2
  N12: S1.Pin_3, S1.Pin_4

custom parts:
  NodeMCU V1.0: ESP8266 based NodeMCU
